// Logisim project Atividade2.circ as structural Verilog
module FF (
  input  Set,
  input  CLK,
  input  Reset,
  output Q,
  output Ql
);

  wire nand_1_out, nand_2_out;

  nand nand_1 (nand_1_out, Set, CLK);
  nand nand_2 (nand_2_out, CLK, Reset);
  nand nand_3 (Q, nand_1_out, Ql);
  nand nand_4 (Ql, Q, nand_2_out);

  // Notes on the sheet:
  //   Flip-Flop Reset Set c/ Clock
endmodule

module FF_JK (
  input  J,
  input  CLK,
  input  K,
  output Q,
  output Ql
);

  wire nand_1_out, nand_2_out;

  nand nand_1 (nand_1_out, J, CLK, Ql);
  nand nand_2 (nand_2_out, Q, CLK, K);
  nand nand_3 (Q, nand_1_out, Ql);
  nand nand_4 (Ql, Q, nand_2_out);

  // Notes on the sheet:
  //   Flip-Flop JK
endmodule

module FF_JK_PC (
  input  PRESET,
  input  J,
  input  CLK,
  input  K,
  input  CLEAR,
  output Q,
  output Ql
);

  wire nand_1_out, nand_2_out, not_1_out, not_2_out;

  nand nand_1 (nand_1_out, J, CLK, Ql);
  nand nand_2 (nand_2_out, Q, CLK, K);
  not not_1 (not_1_out, PRESET);
  not not_2 (not_2_out, CLEAR);
  nand nand_3 (Q, not_1_out, nand_1_out, Ql);
  nand nand_4 (Ql, Q, nand_2_out, not_2_out);

  // Notes on the sheet:
  //   Flip-Flop JK com Entrada Preset e Clear
endmodule

module FF_JK_ME_PC (
  input  PRESET,
  input  J,
  input  CLK,
  input  K,
  input  CLEAR,
  output Q,
  output Qq
);

  wire nand_1_out, nand_2_out, nand_3_out, nand_4_out, nand_5_out, nand_6_out, not_1_out, not_2_out,
       not_3_out;

  nand nand_1 (nand_1_out, J, CLK, Qq);
  nand nand_2 (nand_2_out, Q, CLK, K);
  not not_1 (not_1_out, PRESET);
  not not_2 (not_2_out, CLEAR);
  nand nand_3 (nand_3_out, not_1_out, nand_1_out, nand_4_out);
  nand nand_4 (nand_4_out, nand_3_out, nand_2_out, not_2_out);
  not not_3 (not_3_out, CLK);
  nand nand_5 (nand_5_out, nand_3_out, not_3_out);
  nand nand_6 (nand_6_out, not_3_out, nand_4_out);
  nand nand_7 (Q, not_1_out, nand_5_out, Qq);
  nand nand_8 (Qq, Q, nand_6_out, not_2_out);

  // Notes on the sheet:
  //   Flip-Flop JK Mestre-Escravo com Entrada Preset e Clear
endmodule

module FF_JK_ME_PC_T (
  input  PRESET,
  input  J,
  input  CLK,
  input  CLEAR,
  output Q,
  output Qq
);

  wire nand_1_out, nand_2_out, nand_3_out, nand_4_out, nand_5_out, nand_6_out, not_1_out, not_2_out,
       not_3_out;

  nand nand_1 (nand_1_out, J, CLK, Qq);
  nand nand_2 (nand_2_out, Q, CLK, J);
  not not_1 (not_1_out, PRESET);
  not not_2 (not_2_out, CLEAR);
  nand nand_3 (nand_3_out, not_1_out, nand_1_out, nand_4_out);
  nand nand_4 (nand_4_out, nand_3_out, nand_2_out, not_2_out);
  not not_3 (not_3_out, CLK);
  nand nand_5 (nand_5_out, nand_3_out, not_3_out);
  nand nand_6 (nand_6_out, not_3_out, nand_4_out);
  nand nand_7 (Q, not_1_out, nand_5_out, Qq);
  nand nand_8 (Qq, Q, nand_6_out, not_2_out);

  // Notes on the sheet:
  //   Flip-Flop JK Mestre-Escravo com Entrada Preset e Clear T
endmodule

module FF_JK_ME_PC_D (
  input  PRESET,
  input  J,
  input  CLK,
  input  CLEAR,
  output Q,
  output Qq
);

  wire nand_1_out, nand_2_out, nand_3_out, nand_4_out, nand_5_out, nand_6_out, not_1_out, not_2_out,
       not_3_out, not_4_out;

  not not_1 (not_1_out, J);
  nand nand_1 (nand_1_out, J, CLK, Qq);
  nand nand_2 (nand_2_out, Q, CLK, not_1_out);
  not not_2 (not_2_out, PRESET);
  not not_3 (not_3_out, CLEAR);
  nand nand_3 (nand_3_out, not_2_out, nand_1_out, nand_4_out);
  nand nand_4 (nand_4_out, nand_3_out, nand_2_out, not_3_out);
  not not_4 (not_4_out, CLK);
  nand nand_5 (nand_5_out, nand_3_out, not_4_out);
  nand nand_6 (nand_6_out, not_4_out, nand_4_out);
  nand nand_7 (Q, not_2_out, nand_5_out, Qq);
  nand nand_8 (Qq, Q, nand_6_out, not_3_out);

  // Notes on the sheet:
  //   Flip-Flop JK Mestre-Escravo com Entrada Preset e Clear T
endmodule

module DivisorDeFrenquencia (
  input  PRESET,
  input  J,
  input  CLEAR,
  output out_4,
  output out_5,
  output out_6,
  output out_7
);

  wire CLK_out, ff_jk_me_pc_t_1_qq, ff_jk_me_pc_t_2_qq, ff_jk_me_pc_t_3_qq, ff_jk_me_pc_t_4_qq;
  wire [6:0] decodificador_hex_1_out_2;

  Clock CLK (.out(CLK_out));
  decodificador_hex decodificador_hex_1 (.in_1({out_7, out_6, out_5, out_4}), .out_2(decodificador_hex_1_out_2));
  _7_Segment_Display u_7_segment_display_1 (
    .g(decodificador_hex_1_out_2[6]), .f(decodificador_hex_1_out_2[5]), .a(decodificador_hex_1_out_2[0]),
    .b(decodificador_hex_1_out_2[1]), .e(decodificador_hex_1_out_2[4]), .d(decodificador_hex_1_out_2[3]),
    .c(decodificador_hex_1_out_2[2]));  // open: dp
  FF_JK_ME_PC_T ff_jk_me_pc_t_1 (
    .PRESET(PRESET), .J(J), .CLK(CLK_out), .CLEAR(CLEAR), .Q(out_4), .Qq(ff_jk_me_pc_t_1_qq));
  // NoConnect on ff_jk_me_pc_t_1_qq
  FF_JK_ME_PC_T ff_jk_me_pc_t_2 (
    .PRESET(PRESET), .J(J), .CLK(out_4), .CLEAR(CLEAR), .Q(out_5), .Qq(ff_jk_me_pc_t_2_qq));
  // NoConnect on ff_jk_me_pc_t_2_qq
  FF_JK_ME_PC_T ff_jk_me_pc_t_3 (
    .PRESET(PRESET), .J(J), .CLK(out_5), .CLEAR(CLEAR), .Q(out_6), .Qq(ff_jk_me_pc_t_3_qq));
  // NoConnect on ff_jk_me_pc_t_3_qq
  FF_JK_ME_PC_T ff_jk_me_pc_t_4 (
    .PRESET(PRESET), .J(J), .CLK(out_6), .CLEAR(CLEAR), .Q(out_7), .Qq(ff_jk_me_pc_t_4_qq));
  // NoConnect on ff_jk_me_pc_t_4_qq

  // Other names for the same wires on the sheet: A[3:0] = {out_7, out_6, out_5, out_4}

  // Notes on the sheet:
  //   Divisor de Frequência com FF_JK_ME_PC_T
endmodule

module decodificador_hex (
  input  [3:0] in_1,
  output [6:0] out_2
);

  wire and_1_out, and_2_out, and_3_out, and_4_out, and_5_out, and_6_out, and_7_out, and_8_out, and_9_out,
       and_10_out, and_11_out, and_12_out, and_13_out, and_14_out, and_15_out, and_16_out, and_17_out,
       and_18_out, and_19_out, and_20_out, and_21_out, and_22_out, and_23_out, and_24_out, and_25_out,
       and_26_out, and_27_out, and_28_out, and_29_out, and_30_out, and_31_out, and_32_out, and_33_out,
       and_34_out, and_35_out, not_1_out, not_2_out, not_3_out, not_4_out;

  not not_1 (not_1_out, in_1[3]);
  not not_2 (not_2_out, in_1[2]);
  not not_3 (not_3_out, in_1[1]);
  not not_4 (not_4_out, in_1[0]);
  and and_1 (and_1_out, not_2_out, not_4_out);
  and and_2 (and_2_out, not_1_out, in_1[1]);
  and and_3 (and_3_out, not_1_out, in_1[2], in_1[0]);
  and and_4 (and_4_out, in_1[3], not_2_out, not_3_out);
  and and_5 (and_5_out, in_1[3], not_4_out);
  and and_6 (and_6_out, in_1[2], in_1[1]);
  and and_7 (and_7_out, not_1_out, not_3_out, not_4_out);
  and and_8 (and_8_out, not_1_out, in_1[1], in_1[0]);
  and and_9 (and_9_out, not_2_out, not_4_out);
  and and_10 (and_10_out, in_1[3], not_3_out, in_1[0]);
  and and_11 (and_11_out, not_1_out, not_2_out);
  and and_12 (and_12_out, not_1_out, in_1[2]);
  and and_13 (and_13_out, in_1[3], not_2_out);
  and and_14 (and_14_out, not_3_out, in_1[0]);
  and and_15 (and_15_out, not_2_out, not_3_out);
  and and_16 (and_16_out, not_2_out, in_1[0]);
  and and_17 (and_17_out, in_1[2], not_3_out, in_1[0]);
  and and_18 (and_18_out, not_1_out, not_2_out, not_4_out);
  and and_19 (and_19_out, not_2_out, in_1[1], in_1[0]);
  and and_20 (and_20_out, in_1[3], not_3_out);
  and and_21 (and_21_out, in_1[2], in_1[1], not_4_out);
  and and_22 (and_22_out, not_2_out, not_4_out);
  and and_23 (and_23_out, in_1[1], not_4_out);
  and and_24 (and_24_out, in_1[3], in_1[1]);
  and and_25 (and_25_out, in_1[3], in_1[2]);
  and and_26 (and_26_out, not_3_out, not_4_out);
  and and_27 (and_27_out, not_1_out, in_1[2], not_3_out);
  and and_28 (and_28_out, in_1[2], not_4_out);
  and and_29 (and_29_out, in_1[3], not_2_out);
  and and_30 (and_30_out, in_1[3], in_1[1]);
  and and_31 (and_31_out, not_2_out, in_1[1]);
  and and_32 (and_32_out, in_1[3], not_2_out);
  and and_33 (and_33_out, not_1_out, in_1[2], not_3_out);
  and and_34 (and_34_out, in_1[1], not_4_out);
  and and_35 (and_35_out, in_1[3], in_1[0]);
  or or_1 (out_2[0], and_1_out, and_2_out, and_3_out, and_4_out, and_5_out, and_6_out);
  or or_2 (out_2[1], and_7_out, and_8_out, and_9_out, and_10_out, and_11_out);
  or or_3 (out_2[2], and_12_out, and_13_out, and_14_out, and_15_out, and_16_out);
  or or_4 (out_2[3], and_17_out, and_18_out, and_19_out, and_20_out, and_21_out);
  or or_5 (out_2[4], and_22_out, and_23_out, and_24_out, and_25_out);
  or or_6 (out_2[5], and_26_out, and_27_out, and_28_out, and_29_out, and_30_out);
  or or_7 (out_2[6], and_31_out, and_32_out, and_33_out, and_34_out, and_35_out);
endmodule
