// Logisim project trabalhoFinal1.circ as structural Verilog
module main (
  input  [2:0] sel,
  input  [3:0] A,
  input  [3:0] B,
  output [3:0] S
);

  menu_logico menu_logico_1 (.sel(sel), .A(A), .B(B), .S(S));
endmodule

module menu_logico (
  input  [2:0] sel,
  input  [3:0] A,
  input  [3:0] B,
  output [3:0] S
);

  wire seletor_1_sig0, seletor_1_sig1, seletor_1_sig2, seletor_1_sig3, seletor_1_sig4, seletor_1_sig5,
       seletor_1_sig6, seletor_1_sig7;
  wire [3:0] adder_000_1_s, and_011_1_s, gerador_de_paridade_111_1_s, mascara_ligar_101_1_s,
       mascara_modificar_110_1_s, or_100_1_s, subtractor_001_1_s, twocomplementsub_010_1_s;

  seletor seletor_1 (
    .sel(sel), .sig0(seletor_1_sig0), .sig1(seletor_1_sig1), .sig2(seletor_1_sig2), .sig3(seletor_1_sig3),
    .sig4(seletor_1_sig4), .sig5(seletor_1_sig5), .sig6(seletor_1_sig6), .sig7(seletor_1_sig7));
  Hex_Digit_Display hex_digit_display_1 (.value({1'b0, sel}));  // open: dp
  Hex_Digit_Display hex_digit_display_2 (.value(A));  // open: dp
  Hex_Digit_Display hex_digit_display_3 (.value(B));  // open: dp
  Hex_Digit_Display hex_digit_display_4 (.value(S));  // open: dp
  adder_000 adder_000_1 (.sig(seletor_1_sig0), .A(A), .B(B), .S(adder_000_1_s));
  subtractor_001 subtractor_001_1 (.sig(seletor_1_sig1), .A(A), .B(B), .S(subtractor_001_1_s));
  twocomplementsub_010 twocomplementsub_010_1 (.sig(seletor_1_sig2), .A(A), .B(B), .S(twocomplementsub_010_1_s));
  and_011 and_011_1 (.sig(seletor_1_sig3), .A(A), .B(B), .S(and_011_1_s));
  or_100 or_100_1 (.sig(seletor_1_sig4), .A(A), .B(B), .S(or_100_1_s));
  mascara_ligar_101 mascara_ligar_101_1 (.sig(seletor_1_sig5), .A(A), .B(B), .S(mascara_ligar_101_1_s));
  mascara_modificar_110 mascara_modificar_110_1 (.sig(seletor_1_sig6), .A(A), .B(B), .S(mascara_modificar_110_1_s));
  gerador_de_paridade_111 gerador_de_paridade_111_1 (
    .sig(seletor_1_sig7), .A(A), .B(B), .S(gerador_de_paridade_111_1_s));
  big_or big_or_1 (
    .S0(adder_000_1_s), .S1(subtractor_001_1_s), .S2(twocomplementsub_010_1_s), .S3(and_011_1_s),
    .S4(or_100_1_s), .S5(mascara_ligar_101_1_s), .S6(mascara_modificar_110_1_s),
    .S7(gerador_de_paridade_111_1_s), .S(S));

  // Notes on the sheet:
  //   Seletor
  //   operação
  //   Menu de Operações Lógicas
  //   entradas
  //   Operações Lógicas
  //   saída
  //   =
  //   Filtro de Saídas
endmodule

module seletor (
  input  [2:0] sel,
  output sig0,
  output sig1,
  output sig2,
  output sig3,
  output sig4,
  output sig5,
  output sig6,
  output sig7
);

  and and_1 (sig0, ~sel[2], ~sel[1], ~sel[0]);  // AND_Gate
  and and_2 (sig1, ~sel[2], ~sel[1], sel[0]);  // AND_Gate
  and and_3 (sig2, ~sel[2], sel[1], ~sel[0]);  // AND_Gate
  and and_4 (sig3, ~sel[2], sel[1], sel[0]);  // AND_Gate
  and and_5 (sig4, sel[2], ~sel[1], ~sel[0]);  // AND_Gate
  and and_6 (sig5, sel[2], ~sel[1], sel[0]);  // AND_Gate
  and and_7 (sig6, sel[2], sel[1], ~sel[0]);  // AND_Gate
  and and_8 (sig7, sel[2], sel[1], sel[0]);
endmodule

module adder_000 (
  input  sig,
  input  [3:0] A,
  input  [3:0] B,
  output [3:0] S
);

  wire A0_out, A1_out, A2_out, A3_out, B0_out, B1_out, B2_out, B3_out, full_adder_1_cout, full_adder_2_cout,
       full_adder_3_cout, full_adder_4_cout;

  and A3 (A3_out, A[3], sig);
  and A2 (A2_out, A[2], sig);
  full_adder full_adder_1 (.A(A3_out), .B(B3_out), .Cin(full_adder_2_cout), .S(S[3]), .Cout(full_adder_1_cout));
  and A1 (A1_out, A[1], sig);
  and A0 (A0_out, A[0], sig);
  full_adder full_adder_2 (.A(A2_out), .B(B2_out), .Cin(full_adder_3_cout), .S(S[2]), .Cout(full_adder_2_cout));
  and B3 (B3_out, B[3], sig);
  and B2 (B2_out, B[2], sig);
  full_adder full_adder_3 (.A(A1_out), .B(B1_out), .Cin(full_adder_4_cout), .S(S[1]), .Cout(full_adder_3_cout));
  and B1 (B1_out, B[1], sig);
  and B0 (B0_out, B[0], sig);
  full_adder full_adder_4 (.A(A0_out), .B(B0_out), .Cin(1'b0), .S(S[0]), .Cout(full_adder_4_cout));
  // also tied to GND on the sheet: full_adder_1_cout
endmodule

module subtractor_001 (
  input  sig,
  input  [3:0] A,
  input  [3:0] B,
  output [3:0] S
);

  wire A0_out, A1_out, A2_out, A3_out, B0_out, B1_out, B2_out, B3_out, full_subtractor_1_cout,
       full_subtractor_2_cout, full_subtractor_3_cout, full_subtractor_4_cout;

  and A3 (A3_out, A[3], sig);
  and A2 (A2_out, A[2], sig);
  full_subtractor full_subtractor_1 (
    .A(A3_out), .B(B3_out), .Cin(full_subtractor_2_cout), .S(S[3]), .Cout(full_subtractor_1_cout));
  and A1 (A1_out, A[1], sig);
  and A0 (A0_out, A[0], sig);
  full_subtractor full_subtractor_2 (
    .A(A2_out), .B(B2_out), .Cin(full_subtractor_3_cout), .S(S[2]), .Cout(full_subtractor_2_cout));
  and B3 (B3_out, B[3], sig);
  and B2 (B2_out, B[2], sig);
  full_subtractor full_subtractor_3 (
    .A(A1_out), .B(B1_out), .Cin(full_subtractor_4_cout), .S(S[1]), .Cout(full_subtractor_3_cout));
  and B1 (B1_out, B[1], sig);
  and B0 (B0_out, B[0], sig);
  full_subtractor full_subtractor_4 (.A(A0_out), .B(B0_out), .Cin(1'b0), .S(S[0]), .Cout(full_subtractor_4_cout));
  // also tied to GND on the sheet: full_subtractor_1_cout
endmodule

module twocomplementsub_010 (
  input  sig,
  input  [3:0] A,
  input  [3:0] B,
  output [3:0] S
);

  wire A0_out, A1_out, A2_out, A3_out, and_1_out, B0_out, B1_out, B2_out, B3_out, full_adder_1_cout,
       full_adder_2_cout, full_adder_3_cout, full_adder_4_cout, not_1_out, not_2_out, not_3_out, not_4_out;

  and A3 (A3_out, A[3], sig);
  and A2 (A2_out, A[2], sig);
  full_adder full_adder_1 (.A(A3_out), .B(B3_out), .Cin(full_adder_2_cout), .S(S[3]), .Cout(full_adder_1_cout));
  and A1 (A1_out, A[1], sig);
  and A0 (A0_out, A[0], sig);
  full_adder full_adder_2 (.A(A2_out), .B(B2_out), .Cin(full_adder_3_cout), .S(S[2]), .Cout(full_adder_2_cout));
  not not_1 (not_1_out, B[3]);
  not not_2 (not_2_out, B[2]);
  and B3 (B3_out, not_1_out, sig);
  and B2 (B2_out, not_2_out, sig);
  full_adder full_adder_3 (.A(A1_out), .B(B1_out), .Cin(full_adder_4_cout), .S(S[1]), .Cout(full_adder_3_cout));
  not not_3 (not_3_out, B[1]);
  not not_4 (not_4_out, B[0]);
  and B1 (B1_out, not_3_out, sig);
  and B0 (B0_out, not_4_out, sig);
  and and_1 (and_1_out, sig, 1'b1);
  full_adder full_adder_4 (.A(A0_out), .B(B0_out), .Cin(and_1_out), .S(S[0]), .Cout(full_adder_4_cout));
  // also tied to GND on the sheet: full_adder_1_cout
endmodule

module and_011 (
  input  sig,
  input  [3:0] A,
  input  [3:0] B,
  output [3:0] S
);

  wire S0_out, S1_out, S2_out, S3_out;

  and S3 (S3_out, B[3], A[3]);
  and S2 (S2_out, B[2], A[2]);
  and and_1 (S[2], S2_out, sig);
  and and_2 (S[3], S3_out, sig);
  and S1 (S1_out, B[1], A[1]);
  and S0 (S0_out, A[0], B[0]);
  and and_3 (S[0], S0_out, sig);
  and and_4 (S[1], S1_out, sig);
endmodule

module or_100 (
  input  sig,
  input  [3:0] A,
  input  [3:0] B,
  output [3:0] S
);

  wire S0_out, S1_out, S2_out, S3_out;

  or S3 (S3_out, B[3], A[3]);
  or S2 (S2_out, B[2], A[2]);
  and and_1 (S[2], S2_out, sig);
  and and_2 (S[3], S3_out, sig);
  or S1 (S1_out, B[1], A[1]);
  or S0 (S0_out, A[0], B[0]);
  and and_3 (S[0], S0_out, sig);
  and and_4 (S[1], S1_out, sig);
endmodule

module mascara_ligar_101 (
  input  sig,
  input  [3:0] A,
  input  [3:0] B,
  output [3:0] S
);

  wire S0_out, S1_out, S2_out, S3_out;

  or S3 (S3_out, B[3], A[3]);
  or S2 (S2_out, B[2], A[2]);
  and and_1 (S[2], S2_out, sig);
  and and_2 (S[3], S3_out, sig);
  or S1 (S1_out, B[1], A[1]);
  or S0 (S0_out, A[0], B[0]);
  and and_3 (S[0], S0_out, sig);
  and and_4 (S[1], S1_out, sig);
endmodule

module mascara_modificar_110 (
  input  sig,
  input  [3:0] A,
  input  [3:0] B,
  output [3:0] S
);

  wire xor_1_out, xor_2_out, xor_3_out, xor_4_out;

  xor xor_1 (xor_1_out, B[3], A[3]);
  xor xor_2 (xor_2_out, B[2], A[2]);
  and and_1 (S[2], xor_2_out, sig);
  and and_2 (S[3], xor_1_out, sig);
  xor xor_3 (xor_3_out, B[1], A[1]);
  xor xor_4 (xor_4_out, A[0], B[0]);
  and and_3 (S[0], xor_4_out, sig);
  and and_4 (S[1], xor_3_out, sig);
endmodule

module gerador_de_paridade_111 (
  input  sig,
  input  [3:0] A,
  input  [3:0] B,
  output [3:0] S
);

  wire and_1_out, and_2_out, and_3_out, and_4_out, not_1_out, not_2_out, xor_1_out, xor_2_out;

  not not_1 (not_1_out, A[3]);
  and and_1 (and_1_out, not_1_out, sig);
  and and_2 (and_2_out, A[2], sig);
  xor xor_1 (xor_1_out, and_1_out, and_2_out);
  not not_2 (not_2_out, A[1]);
  and and_3 (and_3_out, not_2_out, sig);
  and and_4 (and_4_out, A[0], sig);
  xor xor_2 (xor_2_out, and_3_out, and_4_out);
  xor xor_3 (S[0], xor_1_out, xor_2_out);

  assign B[2:0] = {3{B[3]}};
  assign S[3:1] = 3'b000;
  // also tied to GND on the sheet: B[3]
endmodule

module full_adder (
  input  A,
  input  B,
  input  Cin,
  output S,
  output Cout
);

  wire and_1_out, and_2_out, and_3_out, xor_1_out;

  xor xor_1 (xor_1_out, A, B);
  and and_1 (and_1_out, A, B);
  and and_2 (and_2_out, A, Cin);
  and and_3 (and_3_out, B, Cin);
  xor xor_2 (S, xor_1_out, Cin);
  or or_1 (Cout, and_1_out, and_2_out, and_3_out);

  // Notes on the sheet:
  //   S = (A ⊕ B) ⊕ Cin
  //   Cout = (A . B) + (A . Cin) + (B . Cin)
endmodule

module full_subtractor (
  input  A,
  input  B,
  input  Cin,
  output S,
  output Cout
);

  wire and_1_out, and_2_out, and_3_out, not_1_out, xor_1_out;

  not not_1 (not_1_out, A);
  xor xor_1 (xor_1_out, A, B);
  and and_1 (and_1_out, not_1_out, B);
  and and_2 (and_2_out, not_1_out, Cin);
  and and_3 (and_3_out, B, Cin);
  xor xor_2 (S, xor_1_out, Cin);
  or or_1 (Cout, and_1_out, and_2_out, and_3_out);

  // Notes on the sheet:
  //   S = (A ⊕ B) ⊕ Cin
  //   Cout = (A' . B) + (A' . Cin) + (B . Cin)
endmodule

module big_or (
  input  [3:0] S0,
  input  [3:0] S1,
  input  [3:0] S2,
  input  [3:0] S3,
  input  [3:0] S4,
  input  [3:0] S5,
  input  [3:0] S6,
  input  [3:0] S7,
  output [3:0] S
);

  wire [3:0] or_1_out, or_2_out, or_3_out, or_5_out, or_6_out, or_7_out;

  assign or_1_out = S0 | S1;  // OR_Gate or_1, 4 bits wide
  assign or_2_out = S2 | S3;  // OR_Gate or_2, 4 bits wide
  assign or_3_out = or_1_out | or_2_out;  // OR_Gate or_3, 4 bits wide
  assign S = or_3_out | or_6_out;  // OR_Gate or_4, 4 bits wide
  assign or_5_out = S4 | S5;  // OR_Gate or_5, 4 bits wide
  assign or_6_out = or_5_out | or_7_out;  // OR_Gate or_6, 4 bits wide
  assign or_7_out = S6 | S7;  // OR_Gate or_7, 4 bits wide
endmodule

module main_vhdl (
  input  [2:0] sel,
  input  [3:0] A,
  input  [3:0] B,
  output [3:0] S
);

  menu_logico_vhdl menu_logico_vhdl_1 (.sel(sel), .A(A), .B(B), .S(S));
endmodule

module menu_logico_vhdl (
  input  [2:0] sel,
  input  [3:0] A,
  input  [3:0] B,
  output [3:0] S
);

  wire seletor_vhdl_1_sig0, seletor_vhdl_1_sig1, seletor_vhdl_1_sig2, seletor_vhdl_1_sig3,
       seletor_vhdl_1_sig4, seletor_vhdl_1_sig5, seletor_vhdl_1_sig6, seletor_vhdl_1_sig7;
  wire [3:0] adder_000_vhdl_1_s, and_011_vhdl_1_s, gerador_de_paridade_111_vhdl_1_s,
       mascara_ligar_101_vhdl_1_s, mascara_modificar_110_vhdl_1_s, or_100_vhdl_1_s, subtractor_001_vhdl_1_s,
       twocomplementsub_010_vhdl_1_s;

  seletor_vhdl seletor_vhdl_1 (
    .sel(sel), .sig0(seletor_vhdl_1_sig0), .sig1(seletor_vhdl_1_sig1), .sig2(seletor_vhdl_1_sig2),
    .sig3(seletor_vhdl_1_sig3), .sig4(seletor_vhdl_1_sig4), .sig5(seletor_vhdl_1_sig5),
    .sig6(seletor_vhdl_1_sig6), .sig7(seletor_vhdl_1_sig7));
  Hex_Digit_Display hex_digit_display_1 (.value({1'b0, sel}));  // open: dp
  Hex_Digit_Display hex_digit_display_2 (.value(A));  // open: dp
  Hex_Digit_Display hex_digit_display_3 (.value(B));  // open: dp
  Hex_Digit_Display hex_digit_display_4 (.value(S));  // open: dp
  adder_000_vhdl adder_000_vhdl_1 (.sig(seletor_vhdl_1_sig0), .A(A), .B(B), .S(adder_000_vhdl_1_s));
  subtractor_001_vhdl subtractor_001_vhdl_1 (.sig(seletor_vhdl_1_sig1), .A(A), .B(B), .S(subtractor_001_vhdl_1_s));
  twocomplementsub_010_vhdl twocomplementsub_010_vhdl_1 (
    .sig(seletor_vhdl_1_sig2), .A(A), .B(B), .S(twocomplementsub_010_vhdl_1_s));
  and_011_vhdl and_011_vhdl_1 (.sig(seletor_vhdl_1_sig3), .A(A), .B(B), .S(and_011_vhdl_1_s));
  or_100_vhdl or_100_vhdl_1 (.sig(seletor_vhdl_1_sig4), .A(A), .B(B), .S(or_100_vhdl_1_s));
  mascara_ligar_101_vhdl mascara_ligar_101_vhdl_1 (
    .sig(seletor_vhdl_1_sig5), .A(A), .B(B), .S(mascara_ligar_101_vhdl_1_s));
  mascara_modificar_110_vhdl mascara_modificar_110_vhdl_1 (
    .sig(seletor_vhdl_1_sig6), .A(A), .B(B), .S(mascara_modificar_110_vhdl_1_s));
  gerador_de_paridade_111_vhdl gerador_de_paridade_111_vhdl_1 (
    .sig(seletor_vhdl_1_sig7), .A(A), .B(B), .S(gerador_de_paridade_111_vhdl_1_s));
  big_or_vhdl big_or_vhdl_1 (
    .S0(adder_000_vhdl_1_s), .S1(subtractor_001_vhdl_1_s), .S2(twocomplementsub_010_vhdl_1_s),
    .S3(and_011_vhdl_1_s), .S4(or_100_vhdl_1_s), .S5(mascara_ligar_101_vhdl_1_s),
    .S6(mascara_modificar_110_vhdl_1_s), .S7(gerador_de_paridade_111_vhdl_1_s), .S(S));

  // Notes on the sheet:
  //   Seletor
  //   operação
  //   entradas
  //   Operações Lógicas
  //   saída
  //   =
  //   Filtro de Saídas
endmodule

module adder_000_vhdl (
  input  sig,
  input  [3:0] A,
  input  [3:0] B,
  output [3:0] S
);

  wire A0_out, A1_out, A2_out, A3_out, B0_out, B1_out, B2_out, B3_out, full_adder_vhdl_1_cout,
       full_adder_vhdl_2_cout, full_adder_vhdl_3_cout, full_adder_vhdl_4_cout;

  and A3 (A3_out, A[3], sig);
  and A2 (A2_out, A[2], sig);
  full_adder_vhdl full_adder_vhdl_1 (
    .A(A3_out), .B(B3_out), .Cin(full_adder_vhdl_2_cout), .S(S[3]), .Cout(full_adder_vhdl_1_cout));
  and A1 (A1_out, A[1], sig);
  and A0 (A0_out, A[0], sig);
  full_adder_vhdl full_adder_vhdl_2 (
    .A(A2_out), .B(B2_out), .Cin(full_adder_vhdl_3_cout), .S(S[2]), .Cout(full_adder_vhdl_2_cout));
  and B3 (B3_out, B[3], sig);
  and B2 (B2_out, B[2], sig);
  full_adder_vhdl full_adder_vhdl_3 (
    .A(A1_out), .B(B1_out), .Cin(full_adder_vhdl_4_cout), .S(S[1]), .Cout(full_adder_vhdl_3_cout));
  and B1 (B1_out, B[1], sig);
  and B0 (B0_out, B[0], sig);
  full_adder_vhdl full_adder_vhdl_4 (.A(A0_out), .B(B0_out), .Cin(1'b0), .S(S[0]), .Cout(full_adder_vhdl_4_cout));
  // also tied to GND on the sheet: full_adder_vhdl_1_cout
endmodule

module subtractor_001_vhdl (
  input  sig,
  input  [3:0] A,
  input  [3:0] B,
  output [3:0] S
);

  wire A0_out, A1_out, A2_out, A3_out, B0_out, B1_out, B2_out, B3_out, full_subtractor_vhdl_1_cout,
       full_subtractor_vhdl_2_cout, full_subtractor_vhdl_3_cout, full_subtractor_vhdl_4_cout;

  and A3 (A3_out, A[3], sig);
  and A2 (A2_out, A[2], sig);
  full_subtractor_vhdl full_subtractor_vhdl_1 (
    .A(A3_out), .B(B3_out), .Cin(full_subtractor_vhdl_2_cout), .S(S[3]), .Cout(full_subtractor_vhdl_1_cout));
  and A1 (A1_out, A[1], sig);
  and A0 (A0_out, A[0], sig);
  full_subtractor_vhdl full_subtractor_vhdl_2 (
    .A(A2_out), .B(B2_out), .Cin(full_subtractor_vhdl_3_cout), .S(S[2]), .Cout(full_subtractor_vhdl_2_cout));
  and B3 (B3_out, B[3], sig);
  and B2 (B2_out, B[2], sig);
  full_subtractor_vhdl full_subtractor_vhdl_3 (
    .A(A1_out), .B(B1_out), .Cin(full_subtractor_vhdl_4_cout), .S(S[1]), .Cout(full_subtractor_vhdl_3_cout));
  and B1 (B1_out, B[1], sig);
  and B0 (B0_out, B[0], sig);
  full_subtractor_vhdl full_subtractor_vhdl_4 (
    .A(A0_out), .B(B0_out), .Cin(1'b0), .S(S[0]), .Cout(full_subtractor_vhdl_4_cout));
  // also tied to GND on the sheet: full_subtractor_vhdl_1_cout
endmodule

module twocomplementsub_010_vhdl (
  input  sig,
  input  [3:0] A,
  input  [3:0] B,
  output [3:0] S
);

  wire A0_out, A1_out, A2_out, A3_out, and_1_out, B0_out, B1_out, B2_out, B3_out, full_adder_vhdl_1_cout,
       full_adder_vhdl_2_cout, full_adder_vhdl_3_cout, full_adder_vhdl_4_cout, not_1_out, not_2_out,
       not_3_out, not_4_out;

  and A3 (A3_out, A[3], sig);
  and A2 (A2_out, A[2], sig);
  full_adder_vhdl full_adder_vhdl_1 (
    .A(A3_out), .B(B3_out), .Cin(full_adder_vhdl_2_cout), .S(S[3]), .Cout(full_adder_vhdl_1_cout));
  and A1 (A1_out, A[1], sig);
  and A0 (A0_out, A[0], sig);
  full_adder_vhdl full_adder_vhdl_2 (
    .A(A2_out), .B(B2_out), .Cin(full_adder_vhdl_3_cout), .S(S[2]), .Cout(full_adder_vhdl_2_cout));
  not not_1 (not_1_out, B[3]);
  not not_2 (not_2_out, B[2]);
  and B3 (B3_out, not_1_out, sig);
  and B2 (B2_out, not_2_out, sig);
  full_adder_vhdl full_adder_vhdl_3 (
    .A(A1_out), .B(B1_out), .Cin(full_adder_vhdl_4_cout), .S(S[1]), .Cout(full_adder_vhdl_3_cout));
  not not_3 (not_3_out, B[1]);
  not not_4 (not_4_out, B[0]);
  and B1 (B1_out, not_3_out, sig);
  and B0 (B0_out, not_4_out, sig);
  and and_1 (and_1_out, sig, 1'b1);
  full_adder_vhdl full_adder_vhdl_4 (.A(A0_out), .B(B0_out), .Cin(and_1_out), .S(S[0]), .Cout(full_adder_vhdl_4_cout));
  // also tied to GND on the sheet: full_adder_vhdl_1_cout
endmodule

// VHDL entity seletor_vhdl, as the project stores it:
LIBRARY ieee;
USE ieee.std_logic_1164.all;

ENTITY seletor_vhdl IS
  PORT (
    sel     : IN  std_logic_vector(2 downto 0);
    sig0    : OUT std_logic;
    sig1    : OUT std_logic;
    sig2    : OUT std_logic;
    sig3    : OUT std_logic;
    sig4    : OUT std_logic;
    sig5    : OUT std_logic;
    sig6    : OUT std_logic;
    sig7    : OUT std_logic
  );
END seletor_vhdl;

ARCHITECTURE TypeArchitecture OF seletor_vhdl IS
BEGIN
  PROCESS (sel)
  BEGIN
    sig0 <= '0';
    sig1 <= '0';
    sig2 <= '0';
    sig3 <= '0';
    sig4 <= '0';
    sig5 <= '0';
    sig6 <= '0';
    sig7 <= '0';
    
    CASE sel IS
      WHEN "000" => sig0 <= '1';
      WHEN "001" => sig1 <= '1';
      WHEN "010" => sig2 <= '1';
      WHEN "011" => sig3 <= '1';
      WHEN "100" => sig4 <= '1';
      WHEN "101" => sig5 <= '1';
      WHEN "110" => sig6 <= '1';
      WHEN "111" => sig7 <= '1';
      WHEN OTHERS => NULL;
    END CASE;
  END PROCESS;
END TypeArchitecture;

// VHDL entity and_011_vhdl, as the project stores it:
LIBRARY ieee;
USE ieee.std_logic_1164.all;

ENTITY and_011_vhdl IS
  PORT (
    sig    : IN  std_logic;
    A      : IN  std_logic_vector(3 downto 0);
    B      : IN  std_logic_vector(3 downto 0);
    S      : OUT std_logic_vector(3 downto 0)
  );
END and_011_vhdl;

ARCHITECTURE Behavioral OF and_011_vhdl IS
BEGIN
  PROCESS (A, B, sig)
  BEGIN
    S <= (A AND B) AND (sig & sig & sig & sig);
  END PROCESS;
END Behavioral;

// VHDL entity or_100_vhdl, as the project stores it:
LIBRARY ieee;
USE ieee.std_logic_1164.all;

ENTITY or_100_vhdl IS
  PORT (
    sig    : IN  std_logic;
    A      : IN  std_logic_vector(3 downto 0);
    B      : IN  std_logic_vector(3 downto 0);
    S      : OUT std_logic_vector(3 downto 0)
  );
END or_100_vhdl;

ARCHITECTURE Behavioral OF or_100_vhdl IS
BEGIN
  PROCESS (A, B, sig)
  BEGIN
    S <= (A OR B) AND (sig & sig & sig & sig);
  END PROCESS;
END Behavioral;

// VHDL entity mascara_ligar_101_vhdl, as the project stores it:
LIBRARY ieee;
USE ieee.std_logic_1164.all;

ENTITY mascara_ligar_101_vhdl IS
  PORT (
    sig    : IN  std_logic;
    A      : IN  std_logic_vector(3 downto 0);
    B      : IN  std_logic_vector(3 downto 0);
    S      : OUT std_logic_vector(3 downto 0)
  );
END mascara_ligar_101_vhdl;

ARCHITECTURE Behavioral OF mascara_ligar_101_vhdl IS
BEGIN
  PROCESS (A, B, sig)
  BEGIN
    S <= (A OR B) AND (sig & sig & sig & sig);
  END PROCESS;
END Behavioral;

// VHDL entity mascara_modificar_110_vhdl, as the project stores it:
LIBRARY ieee;
USE ieee.std_logic_1164.all;

ENTITY mascara_modificar_110_vhdl IS
  PORT (
    sig    : IN  std_logic;
    A      : IN  std_logic_vector(3 downto 0);
    B      : IN  std_logic_vector(3 downto 0);
    S      : OUT std_logic_vector(3 downto 0)
  );
END mascara_modificar_110_vhdl;

ARCHITECTURE Behavioral OF mascara_modificar_110_vhdl IS
BEGIN
  PROCESS (A, B, sig)
  BEGIN
    S <= (A XOR B) AND (sig & sig & sig & sig);
  END PROCESS;
END Behavioral;

// VHDL entity gerador_de_paridade_111_vhdl, as the project stores it:
LIBRARY ieee;
USE ieee.std_logic_1164.all;

ENTITY gerador_de_paridade_111_vhdl IS
  PORT (
    sig    : IN  std_logic;
    A      : IN  std_logic_vector(3 downto 0);
    B      : IN  std_logic_vector(3 downto 0);
    S      : OUT std_logic_vector(3 downto 0)
  );
END gerador_de_paridade_111_vhdl;

ARCHITECTURE TypeArchitecture OF gerador_de_paridade_111_vhdl IS
BEGIN
  	S(0) <= (A(0) XOR NOT A(1) XOR A(2) XOR NOT A(3)) AND sig;
  	S(1) <= '0';
  	S(2) <= '0';
  	S(3) <= '0';
END TypeArchitecture;

// VHDL entity full_adder_vhdl, as the project stores it:
LIBRARY ieee;
USE ieee.std_logic_1164.all;

ENTITY full_adder_vhdl IS
  PORT (
    A      : IN  std_logic;
    B      : IN  std_logic;
    Cin    : IN  std_logic;
    S      : OUT std_logic;
    Cout   : OUT std_logic
  );
END full_adder_vhdl;

ARCHITECTURE TypeArchitecture OF full_adder_vhdl IS
BEGIN
  S <= (A XOR B) XOR Cin;
  Cout <= (A AND B) or (A AND Cin) or (B AND Cin);
END TypeArchitecture;

// VHDL entity full_subtractor_vhdl, as the project stores it:
LIBRARY ieee;
USE ieee.std_logic_1164.all;

ENTITY full_subtractor_vhdl IS
  PORT (
    A      : IN  std_logic;
    B      : IN  std_logic;
    Cin    : IN  std_logic;
    S      : OUT std_logic;
    Cout   : OUT std_logic
  );
END full_subtractor_vhdl;

ARCHITECTURE TypeArchitecture OF full_subtractor_vhdl IS
BEGIN
  S <= (A XOR B) XOR Cin;
  Cout <= (NOT A AND B) or (NOT A AND Cin) or (B AND Cin);
END TypeArchitecture;

// VHDL entity big_or_vhdl, as the project stores it:
LIBRARY ieee;
USE ieee.std_logic_1164.all;

ENTITY big_or_vhdl IS
  PORT (
    S0  : IN  std_logic_vector(3 downto 0);
    S1  : IN  std_logic_vector(3 downto 0);
    S2  : IN  std_logic_vector(3 downto 0);
    S3  : IN  std_logic_vector(3 downto 0);
    S4  : IN  std_logic_vector(3 downto 0);
    S5  : IN  std_logic_vector(3 downto 0);
    S6  : IN  std_logic_vector(3 downto 0);
    S7  : IN  std_logic_vector(3 downto 0);
    S   : OUT std_logic_vector(3 downto 0)
  );
END big_or_vhdl;

ARCHITECTURE Behavioral OF big_or_vhdl IS
BEGIN
  PROCESS (S0, S1, S2, S3, S4, S5, S6, S7)
  BEGIN
    S <= S0 OR S1 OR S2 OR S3 OR S4 OR S5 OR S6 OR S7;
  END PROCESS;
END Behavioral;
